// Digital circuit DMux4Way.dig as structural Verilog
module DMux4Way (
  input  in,
  input  sel_1,
  input  sel_0,
  output a,
  output b,
  output c,
  output d
);

  wire dmux_1_a, dmux_1_b;

  Dmux dmux_1 (.in(in), .sel(sel_0), .a(dmux_1_a), .b(dmux_1_b));
  Dmux dmux_2 (.in(dmux_1_a), .sel(sel_1), .a(a), .b(b));
  Dmux dmux_3 (.in(dmux_1_b), .sel(sel_1), .a(c), .b(d));
endmodule
