// Digital circuit DMux8Way.dig as structural Verilog
module DMux8Way (
  input  in,
  input  sel_0,
  input  [1:0] sel_1,
  output a,
  output b,
  output c,
  output d,
  output e,
  output f,
  output g,
  output h
);

  wire demultiplexer_1_out_0, demultiplexer_1_out_1;

  Demultiplexer demultiplexer_1 (.sel(sel_0), .in(in), .out_0(demultiplexer_1_out_0), .out_1(demultiplexer_1_out_1));
  Demultiplexer #(.Selector_Bits(2)) demultiplexer_2 (
    .sel(sel_1), .in(demultiplexer_1_out_0), .out_0(a), .out_1(b), .out_2(c), .out_3(d));
  Demultiplexer #(.Selector_Bits(2)) demultiplexer_3 (
    .sel(sel_1), .in(demultiplexer_1_out_1), .out_0(e), .out_1(f), .out_2(g), .out_3(h));
endmodule
