// Digital circuit Mux4Way16.dig as structural Verilog
module Mux4Way16 (
  input  [15:0] a,
  input  [15:0] b,
  input  [15:0] c,
  input  [15:0] d,
  input  [15:0] SEL0,
  input  [15:0] SEL1,
  output [15:0] out
);

  wire [15:0] and_1_out, and_2_out, and_3_out, and_4_out, not_1_out, not_2_out;

  assign not_1_out = ~SEL0;  // Not not_1, 16 bits wide
  assign not_2_out = ~SEL1;  // Not not_2, 16 bits wide
  assign and_1_out = a & not_1_out & not_2_out;  // And and_1, 16 bits wide
  assign and_2_out = b & SEL0 & not_2_out;  // And and_2, 16 bits wide
  assign and_3_out = c & not_1_out & SEL1;  // And and_3, 16 bits wide
  assign and_4_out = d & SEL0 & SEL1;  // And and_4, 16 bits wide
  assign out = and_1_out | and_2_out | and_3_out | and_4_out;  // Or or_1, 16 bits wide
endmodule
